# Fritzing sketch circuit (saved by Fritzing 0.9.1b)

parts:
  Raspberry_Pi1 = Raspberry Pi B+
  RGB_SMD_LED1 = SMD RGB LED (WS2812) [package=5050]
  C1 = Capacitor Polarized [package=cpol-radial-10uf-25v]

nets:
  N1: Raspberry_Pi1.GPIO18, RGB_SMD_LED1.DIn
  N2: RGB_SMD_LED1.DOut, C1.-
